# Fritzing sketch alarm_clock (saved by Fritzing 0.7.1b)
breadboards: 1

parts:
  Arduino1 = Arduino
  S1 = Pushbutton [package="[THT]"]
  U1 = mystery part, 12 pins [chip_label=quad-7segment spacing=700mil]
  R1 = Resistor [tolerance=±5% resistance=330 package=THT]
  R2 = Resistor [tolerance=±5% resistance=330 package=THT]
  R3 = Resistor [tolerance=±5% resistance=330 package=THT]
  R4 = Resistor [tolerance=±5% resistance=330 package=THT]
  R5 = Resistor [tolerance=±5% resistance=10k package=THT]
  R6 = Resistor [tolerance=±5% resistance=10k package=THT]
  R7 = Resistor [tolerance=±5% resistance=10k package=THT]
  R8 = Resistor [tolerance=±5% resistance=10k package=THT]
  U2 = 74HC595 [package="DIP16 [THT]"]
  J1 = Piezo Speaker
  R9 = Resistor [tolerance=±5% resistance=10k package=THT]

nets:
  GND: Arduino1.GND, S1.Pin_1, S1.Pin_2, R5.Pin_0, R6.Pin_0, R7.Pin_0, R8.Pin_0, U2.GND, U2.OE, J1.pin1
  N1: Arduino1.D9, S1.Pin_3, S1.Pin_4, R9.Pin_1
  N2: Arduino1.D8, J1.pin2
  N3: Arduino1.D7, U2.SH_CP
  N4: Arduino1.D6, U2.ST_CP
  N5: Arduino1.D4, U2.DS
  +5V: Arduino1.+5V, U2.MR, U2.VCC, R9.Pin_0
  N6: Arduino1.A0, R1.Pin_1
  N7: Arduino1.A1, R2.Pin_1
  N8: Arduino1.A2, R3.Pin_1
  N9: Arduino1.A3, R4.Pin_1
  N10: U1.pin1, U2.Q4
  N11: U1.pin2, U2.Q3
  N12: U1.pin3, U2.Q7
  N13: U1.pin4, U2.Q2
  N14: U1.pin5, U2.Q6
  N15: U1.pin6, R1.Pin_0, R8.Pin_1
  N16: U1.pin7, U2.Q1
  N17: U1.pin8, R2.Pin_0, R7.Pin_1
  N18: U1.pin9, R3.Pin_0, R6.Pin_1
  N19: U1.pin10, U2.Q5
  N20: U1.pin11, U2.Q0
  N21: U1.pin12, R4.Pin_0, R5.Pin_1
